# Fritzing sketch hookup_diagram_edison_pir (saved by Fritzing 0.9.1b)
breadboards: 1

parts:
  Part1 = Intel Edison Arduinobreakout
  PIR1 = PIR sensor
  R1 = Resistor [tolerance=±5% resistance=10k package=THT]

nets:
  N1: Part1.D6_PWM, PIR1.SIG, R1.Pin_1
  5V: Part1.5V, PIR1.VDD, R1.Pin_0
  GND: Part1.GND, PIR1.GND
